// Logisim project F3.5_library.circ as structural Verilog: 2 circuits, main circuit Decoder_2to4
module Decoder_2to4 (
  input  IN0,
  input  IN1,
  input  EN,
  output OUT0,
  output OUT1,
  output OUT2,
  output OUT3
);

  wire not_1_out, not_2_out;

  not not_1 (not_1_out, IN0);
  not not_2 (not_2_out, IN1);
  and and_1 (OUT0, not_1_out, EN, not_2_out);
  and and_2 (OUT1, IN0, EN, not_2_out);
  and and_3 (OUT2, not_1_out, EN, IN1);
  and and_4 (OUT3, IN0, EN, IN1);
endmodule

module Decoder_3to8 (
  input  A0,
  input  A1,
  input  A2,
  output Y0,
  output Y1,
  output Y2,
  output Y3,
  output Y4,
  output Y5,
  output Y6,
  output Y7
);

  wire not_1_out;

  not not_1 (not_1_out, A2);
  Decoder_2to4 decoder_2to4_1 (.IN0(A0), .IN1(A1), .EN(not_1_out), .OUT0(Y0), .OUT1(Y1), .OUT2(Y2), .OUT3(Y3));
  Decoder_2to4 decoder_2to4_2 (.IN0(A0), .IN1(A1), .EN(A2), .OUT0(Y4), .OUT1(Y5), .OUT2(Y6), .OUT3(Y7));
endmodule
